# Fritzing sketch RemoteLigth (saved by Fritzing 0.9.3b)

parts:
  Part3 = Bluetooth HM-10
  HLK-PM2 = HLK-PM12 [part_number=HLK-PM12]  # not connected
  U1 = RELAY-SOLIDSTATE [package=relay-s108t02]
  LED1 = LEDs [package=led10mm]
  Part4 = Arduino Nano (Rev3.0)

nets:
  N1: Part3.RXD, Part4.D3
  N2: Part3.BRK, Part4.D10
  N3: U1.T1, LED1.C
  N4: U1.+, Part4.D4
  N5: U1.-, Part4.GND

notes:
  ~220

custom parts:
  LEDs: LEDs Standard schematic elements and footprints for 5mm, 3mm, 1206, and 0603 sized LEDs. 5mm - Spark Fun Electronics SKU : COM-00529 (and others)
